# Fritzing sketch arduino-ultra-sonic-9-10 (saved by Fritzing 0.9.3b)

parts:
  Part3 = Arduino Uno (Rev3)
  hc-sr1 = hc-sr04

nets:
  N1: Part3.D9_PWM, hc-sr1.Trig
  N2: Part3.D10_PWM/SS, hc-sr1.Echo
  5V: Part3.5V, hc-sr1.VCC
  GND: Part3.GND, hc-sr1.GND
