# Fritzing sketch uss-1k-2k-rpi-2 (saved by Fritzing 0.9.3b)
breadboards: 1

parts:
  Raspberry_Pi_1 = Raspberry Pi 3 [part_number=RPI-3-V1.2]
  hc-sr1 = hc-sr04
  R1 = Resistor [tolerance=±20% resistance=2k package=THT]
  R2 = Resistor [tolerance=±5% resistance=1k package=THT]

nets:
  3V3: Raspberry_Pi_1.3v3, Raspberry_Pi_1.3V3, Raspberry_Pi_1.5V, hc-sr1.VCC
  GND: Raspberry_Pi_1.GPIO3, Raspberry_Pi_1.GND, hc-sr1.GND, R1.Pin_0
  N1: Raspberry_Pi_1.GIPO4, hc-sr1.Trig
  N2: Raspberry_Pi_1.GIPO17, R1.Pin_1, R2.Pin_0
  N3: hc-sr1.Echo, R2.Pin_1
